# Fritzing sketch Nano-0v8 (saved by Fritzing 1.0.1rc)
circuit board: 4.38796cm x 1.85767cm
breadboards: 1

parts:
  Digital = female pin header, 15 pins [form="♀ (female)"]
  Analog = female pin header, 15 pins [form="♀ (female)"]
  D11-TX1-rgb = male pin header, 4 pins [form="♂ (male)"]
  A4-A5-i2c = male pin header, 4 pins [form="♂ (male)"]
  D9-switch = Pushbutton [package=THT]
  D9-resistor = Resistor [tolerance=±5% power=0.25W resistance=1k package=THT]
  GND-piezo = male pin header, 1 pin [form="♂ (male)"]
  A7-piezo = male pin header, 1 pin [form="♂ (male)"]
  5V-jack = male pin header, 1 pin [form="♂ (male)"]
  NC2-jack = male pin header, 1 pin [form="♂ (male)"]  # not connected
  NC1-jack = male pin header, 1 pin [form="♂ (male)"]  # not connected
  GND-jack = male pin header, 2 pins [form="♂ (male)"]

nets:
  N1: Digital.pin2, D11-TX1-rgb.pin2
  N2: Digital.pin4, D9-switch.leg1, D9-resistor.Pin_1
  N3: Digital.pin12, D11-TX1-rgb.pin1, A4-A5-i2c.pin1, D9-switch.leg0, GND-piezo.pin1, GND-jack.pin1, GND-jack.pin2
  N4: Digital.pin15, D11-TX1-rgb.pin3
  N5: Analog.pin2, A4-A5-i2c.pin4, D9-resistor.Pin_0
  N6: Analog.pin8, A4-A5-i2c.pin3
  N7: Analog.pin9, A4-A5-i2c.pin2
  N8: Analog.pin11, A7-piezo.pin1
  N9: Analog.pin12, D11-TX1-rgb.pin4, 5V-jack.pin1

notes:
  Nano 0v8
  GND
  5V
  TX1
  D11
  A5
  A4
  3V3
  A7
  NC
  D9-sw
  D9-1k
  I2C
  RGB
