# Fritzing sketch Nano-Matter-Occupancy-0v2 (saved by Fritzing 1.0.1rc)
circuit board: 6.31cm x 1.86cm
breadboards: 1

parts:
  Digital = female pin header, 15 pins [form="♀ (female)"]
  Analog = female pin header, 15 pins [form="♀ (female)"]
  A7-PB3-switch = Pushbutton [package=THT]
  A7-PB3-resistor = Resistor [tolerance=±5% power=0.25W resistance=1k package=THT]
  A6-PB1-sensor = female pin header, 3 pins [form="♀ (female)"]

nets:
  N1: Digital.pin6, A7-PB3-switch.leg1, A7-PB3-resistor.Pin_1
  N2: Digital.pin7, A6-PB1-sensor.pin3
  N3: Digital.pin12, A7-PB3-switch.leg0, A6-PB1-sensor.pin1
  N4: Analog.pin2, A7-PB3-resistor.Pin_0, A6-PB1-sensor.pin2

notes:
  Nano Occ 0v2
  D7-sw
  D7-1k
  MarJohLoo
  GND
  3V3
  D6
  PIR
